# Fritzing sketch hcsr04-servo-arduino (saved by Fritzing 0.9.2b)
breadboards: 1

parts:
  Part1 = Arduino Uno (Rev3)
  J1 = Basic Servo
  Part2 = SRF05 Ultrasonic Rangefinder

nets:
  N1: Part1.D10_PWM/SS, Part2.Trig
  N2: Part1.D11_PWM/MOSI, Part2.Echo
  N3: Part1.D12/MISO, J1.pulse
  VCC: Part1.5V, J1.vcc, Part2.VCC
  GND: Part1.GND, J1.gnd, Part2.GND
